// Logisim project sop_xnor_3.circ as structural Verilog: 1 circuit, main circuit main
module main (
  input  A,
  input  B,
  output out_3
);

  wire or_1_out, or_2_out;

  or or_1 (or_1_out, ~A, B);  // OR_Gate
  or or_2 (or_2_out, B, ~A);  // OR_Gate
  and and_1 (out_3, or_1_out, or_2_out);
endmodule
