// Logisim project bistabile_v1.circ as structural Verilog: 1 circuit, main circuit Latch SC
module Latch_SC (
  input  Reset,
  input  Set,
  output Q,
  output nQ
);

  nor nor_1 (Q, Reset, nQ);
  nor nor_2 (nQ, Q, Set);
endmodule
