// Logisim project lsfr.circ as structural Verilog: 1 circuit, main circuit main
module main (
  input  Seed,
  input  [3:0] Seed_2
);

  wire c, multiplexer_1_out, multiplexer_2_out, multiplexer_3_out, multiplexer_4_out, xor_1_out;
  wire [3:0] d_ff_1_q;

  Clock clock_1 (.out(c));
  Multiplexer #(.enable("false")) multiplexer_1 (.in0(xor_1_out), .in1(Seed_2[0]), .out(multiplexer_1_out), .sel(Seed));
  D_Flip_Flop d_ff_1 (.clk(c), .D(multiplexer_1_out), .Q(d_ff_1_q[0]));  // open: Qn, preset, en, reset
  Multiplexer #(.enable("false")) multiplexer_2 (
    .in0(d_ff_1_q[0]), .in1(Seed_2[1]), .out(multiplexer_2_out), .sel(Seed));
  Hex_Digit_Display hex_digit_display_1 (.value(d_ff_1_q));  // open: dp
  D_Flip_Flop d_ff_2 (.clk(c), .D(multiplexer_2_out), .Q(d_ff_1_q[1]));  // open: Qn, preset, en, reset
  xor xor_1 (xor_1_out, d_ff_1_q[3], d_ff_1_q[2]);
  Multiplexer #(.enable("false")) multiplexer_3 (
    .in0(d_ff_1_q[1]), .in1(Seed_2[2]), .out(multiplexer_3_out), .sel(Seed));
  D_Flip_Flop d_ff_3 (.clk(c), .D(multiplexer_3_out), .Q(d_ff_1_q[2]));  // open: Qn, preset, en, reset
  D_Flip_Flop d_ff_4 (.clk(c), .D(multiplexer_4_out), .Q(d_ff_1_q[3]));  // open: Qn, preset, en, reset
  Multiplexer #(.enable("false")) multiplexer_4 (
    .in0(d_ff_1_q[2]), .in1(Seed_2[3]), .out(multiplexer_4_out), .sel(Seed));

  // Other names for the same wires on the sheet: S = Seed; s0 = Seed_2[0]; s1 = Seed_2[1]; s2 = Seed_2[2];
  //   s3 = Seed_2[3]
endmodule
