// Logisim project blinker.circ as structural Verilog: 3 circuits, main circuit on-off
module on_off (
  input  on_off_button,
  input  clock,
  output on_off
);

  wire xor_1_out;

  D_Flip_Flop d_ff_1 (.clk(clock), .D(xor_1_out), .Q(on_off));  // open: Qn, preset, en, reset
  xor xor_1 (xor_1_out, on_off, on_off_button);
endmodule

module main (
);

  wire and_1_out, ck, d_ff_1_q, o, or_1_out, p, tunnel, tunnel_t;
  wire [4:0] counter_1_q, level_1_level, subtractor_1_out, xnor_1_out;
  wire [15:0] level_1_out_5;

  Clock clock_1 (.out(ck));
  on_off on_off_1 (.on_off_button(p), .clock(ck), .on_off(o));
  level level_1 (.in_1(tunnel_t), .in_2(tunnel), .ck(ck), .on(o), .out_5(level_1_out_5), .level(level_1_level));
  DotMatrix #(.inputtype("row"), .matrixcols(1), .matrixrows(16)) dotmatrix_1 (
    .row0(level_1_out_5[15]), .row1(level_1_out_5[14]), .row2(level_1_out_5[13]), .row3(level_1_out_5[12]),
    .row4(level_1_out_5[11]), .row5(level_1_out_5[10]), .row6(level_1_out_5[9]), .row7(level_1_out_5[8]),
    .row8(level_1_out_5[7]), .row9(level_1_out_5[6]), .row10(level_1_out_5[5]), .row11(level_1_out_5[4]),
    .row12(level_1_out_5[3]), .row13(level_1_out_5[2]), .row14(level_1_out_5[1]), .row15(level_1_out_5[0]));
  Button on (.out(p));
  Button button (.out(tunnel));
  LED led_1 (.in(o));
  LED blink (.in(d_ff_1_q));
  Button button_2 (.out(tunnel_t));
  Subtractor #(.width(5)) subtractor_1 (.a(5'b10000), .b(level_1_level), .out(subtractor_1_out));  // open: bin, bout
  Counter #(.width(5), .max('h1f)) counter_1 (
    .count(1'b1), .Q(counter_1_q), .clk(ck), .clr(or_1_out));  // open: load, D, carry
  assign xnor_1_out = ~(subtractor_1_out ^ counter_1_q);  // XNOR_Gate xnor_1, 5 bits wide
  or or_1 (or_1_out, d_ff_1_q, tunnel_t, tunnel, ~o);  // OR_Gate
  and and_1 (and_1_out, xnor_1_out[0], xnor_1_out[1], xnor_1_out[2], xnor_1_out[3], xnor_1_out[4]);
  D_Flip_Flop d_ff_1 (.clk(ck), .D(and_1_out), .Q(d_ff_1_q));  // open: Qn, preset, en, reset
endmodule

module level (
  input  in_1,
  input  in_2,
  input  ck,
  input  on,
  output [15:0] out_5,
  output [4:0] level
);

  wire not_1_out, or_1_out;
  wire [16:0] shifter_1_out;
  wire [16:16] not_2_out;

  or or_1 (or_1_out, in_1, in_2);
  not not_1 (not_1_out, on);
  Counter #(.width(5), .max('h10), .ongoal("stay")) counter_1 (
    .load(in_1), .count(or_1_out), .Q(level), .clk(ck), .clr(not_1_out));  // open: D, carry
  Shifter #(.width(17)) shifter_1 (.in({17{1'b1}}), .\dist (level), .out(shifter_1_out));
  assign {not_2_out[16], out_5} = ~shifter_1_out;  // NOT_Gate not_2, 17 bits wide
endmodule
